# Fritzing sketch wiring (saved by Fritzing 0.9.2b)
breadboards: 1

parts:
  Espessif_Serial_Wifi_Modul_1 = ESP8266 ESP01 [part_number=ESP8266 package=THT]
  R1 = Resistor [tolerance=±5% resistance=470 package=THT]
  R2 = Resistor [tolerance=±5% resistance=10k package=THT]
  Q1 = Basic FET N-Channel [package="TO220 [THT]"]
  J1 = Screw terminal - 2 pins [package=THT]
  J2 = Screw terminal - 2 pins [package=THT]
  J3 = Screw terminal - 2 pins [package=THT]
  J4 = screw terminal, 3 pins
  J5 = Screw terminal - 2 pins [package=THT]

nets:
  GND: Espessif_Serial_Wifi_Modul_1.GND, R2.Pin_1, Q1.source, J2.pin1, J3.pin1, J4.pin1, J5.pin2
  N1: Espessif_Serial_Wifi_Modul_1.RXD, J4.pin3
  N2: Espessif_Serial_Wifi_Modul_1.TXD, J4.pin2
  3.3V: Espessif_Serial_Wifi_Modul_1.VCC, Espessif_Serial_Wifi_Modul_1.CH_PD, J3.pin2
  N3: Espessif_Serial_Wifi_Modul_1.GPIO00, J5.pin1
  N4: Espessif_Serial_Wifi_Modul_1.GPIO02, R1.Pin_0
  N5: R1.Pin_1, R2.Pin_0, Q1.gate
  N6: Q1.drain, J1.pin1
  12V: J1.pin2, J2.pin2

notes:
  GND
  TxD
  RxD
  <- To FTDI
  Programming jumper
  +3.3V In
  +12V In
  To LED strobe
  +
  -
  3.3V In
  12V In
  Output to LED strobe
  FTDI

custom parts:
  ESP8266 ESP01: Generic WiFi Module based on the ESP8266 with onboard PCB antenna and UART communications
